# Fritzing sketch ESP8266_starter (saved by Fritzing 0.9.2b)
breadboards: 1

parts:
  U1 = ESP8266 WiFi Module [part_number=ESP8266]
  Part1 = Arduino Uno (Rev3)
  U2 = V_REG_LD1117VXX [package=78xxl]
  LED1 = LED - 5mm [color="Red (633nm)" package="5 mm [THT]"]
  R1 = Resistor [tolerance=±5% resistance=560 package=THT]

nets:
  N1: U1.RXD, Part1.D0/RX
  N2: U1.VCC, U1.CH_PD, U2.OUT
  N3: U1.GPIO_2, LED1.anode
  GND: U1.GND, Part1.GND, U2.GND, R1.Pin_0
  N4: Part1.5V, U2.IN
  N5: LED1.cathode, R1.Pin_1

custom parts:
  ESP8266 WiFi Module: Generic WiFi Module based on the ESP8266 with onboard PCB antenna and UART communications
